# Fritzing sketch schematic (saved by Fritzing 0.9.5d)
breadboards: 1

parts:
  Part1 = Arduino Uno (Rev3)
  LED1 = LED - 5mm [color="Red (633nm)" package="5 mm [THT]"]
  R1 = Resistor [tolerance=±5% resistance=220 package=THT]
  J2 = DHT11 basic temperature-humidity sensor [form="♂ (male)" package=THT]
  e-radionica_com1 = LM393 LDR breakout [part_number=100027]
  YL-83_-_Control_Board2 = YL-83 Rain Sensor - Control Board
  YL-83_-_Detection_Board2 = YL-83 Rain Sensor - Detection Board
  LCD2 = LCD screen
  LCM1602_IIC2 = LCM1602 IIC [part_number="LCM1602 IIC" chip_label="LCM1602 IIC" package="DIP (Dual Inline) [THT]"]
  J3 = Basic Servo

nets (from the breadboard view):
  N1: Part1.D10_PWM/SS, J2.OUT
  N2: Part1.D12/MISO, LED1.anode, R1.Pin_0, R1.Pin_1
  GND: Part1.GND, J2.GND, e-radionica_com1.GND, YL-83_-_Control_Board2.GND, LCM1602_IIC2.GND, J3.gnd
  N3: Part1.D2, YL-83_-_Control_Board2.DO
  N4: Part1.D3_PWM, e-radionica_com1.DO
  N5: Part1.D4, J3.pulse
  VCC: Part1.5V, LED1.cathode, J2.VCC, e-radionica_com1.VCC, YL-83_-_Control_Board2.VCC, LCM1602_IIC2.VCC
  N6: YL-83_-_Control_Board2.POS, YL-83_-_Detection_Board2.POS
  N7: YL-83_-_Control_Board2.NEG, YL-83_-_Detection_Board2.NEG
  VSS: LCD2.VSS, LCM1602_IIC2.VSS
  VDD: LCD2.VDD, LCM1602_IIC2.VDD
  N8: LCD2.V0, LCM1602_IIC2.V0
  N9: LCD2.RS, LCM1602_IIC2.RS
  N10: LCD2.R/W, LCM1602_IIC2.RW
  N11: LCD2.E, LCM1602_IIC2.E
  N12: LCD2.DB0, LCM1602_IIC2.D0
  N13: LCD2.DB1, LCM1602_IIC2.D1
  N14: LCD2.DB2, LCM1602_IIC2.D2
  N15: LCD2.DB3, LCM1602_IIC2.D3
  N16: LCD2.DB4, LCM1602_IIC2.D4
  N17: LCD2.DB5, LCM1602_IIC2.D5
  N18: LCD2.DB6, LCM1602_IIC2.D6
  N19: LCD2.DB7, LCM1602_IIC2.D7
  N20: LCD2.LED+, LCM1602_IIC2.A
  N21: LCD2.LED-, LCM1602_IIC2.K
  N22: LCM1602_IIC2.LED_A, LCM1602_IIC2.LED_B

custom parts:
  DHT11 basic temperature-humidity sensor: The DHT11 is a basic, ultra low-cost digital temperature and humidity sensor. It uses a capacitive humidity sensor and a thermistor to measure the surrounding air, and spits out a digital signal on the data pin (no analog input pins needed). Its fairly simple to use, but requires careful timing to grab data. The only real downside of this sensor is you can only get new data from it once every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
  YL-83 Rain Sensor - Control Board: The YL-83 is a rain sensor that has more resistance when dry and less resistance when wet. The module runs at 5V.
  YL-83 Rain Sensor - Detection Board: The YL-83 is a rain sensor that has more resistance when dry and less resistance when wet. The module runs at 5V.
  LCM1602 IIC: I2C-Module to use a 1602 or 2004 LCD on with the wire.h libory Serial LCD Modul
